// Logisim project CPU.circ as structural Verilog: 9 circuits, main circuit CPU
module CPU (
  input  rst_btn
);

  wire alu_1_sf, alu_1_zf, clk, controller_1_alub_sel, controller_1_br_sel, controller_1_pc_sel,
       controller_1_ram_we, controller_1_rf_we, multiplexer_4_out;
  wire [1:0] controller_1_npc_op;
  wire [2:0] controller_1_rf_wsel, controller_1_sext_op;
  wire [3:0] controller_1_alu_op;
  wire [11:0] irom_1_inst;
  wire [19:0] irom_1_inst_2;
  wire [31:0] alu_1_c, bit_extender_1_out, dram_1_rdo, multiplexer_1_out, multiplexer_2_out,
       multiplexer_3_out, npc_1_npc, npc_1_pc4, npc_1_pcb, pc_1_pc, rf_1_rd1, rf_1_rd2, sext_1_ext;

  Clock #(.highDuration(1), .lowDuration(1)) clock_1 (.out(clk));
  NPC npc_1 (
    .PC(pc_1_pc), .offset(sext_1_ext), .br(multiplexer_4_out), .op(controller_1_npc_op), .pc4(npc_1_pc4),
    .pcb(npc_1_pcb), .npc(npc_1_npc));
  PC pc_1 (.rst(rst_btn), .din(multiplexer_1_out), .pc(pc_1_pc), .clk(clk));
  Multiplexer #(.select(1), .width(32), .disabled("Z"), .enable("false")) multiplexer_1 (
    .in0(npc_1_npc), .in1(alu_1_c), .out(multiplexer_1_out), .sel(controller_1_pc_sel));
  IROM irom_1 (.adr(pc_1_pc), .inst({irom_1_inst_2, irom_1_inst}));
  SEXT sext_1 (.op(controller_1_sext_op), .din(irom_1_inst_2), .ext(sext_1_ext));
  Multiplexer #(.select(3), .width(32), .disabled("Z"), .enable("false")) multiplexer_2 (
    .in0(alu_1_c), .in1(bit_extender_1_out), .in2(dram_1_rdo), .in3(npc_1_pc4), .in4(sext_1_ext),
    .in5(npc_1_pcb), .out(multiplexer_2_out), .sel(controller_1_rf_wsel));  // open: in6, in7
  assign bit_extender_1_out = {{31{1'b0}}, multiplexer_4_out};  // Bit_Extender bit_extender_1
  Controller controller_1 (
    .opcode(irom_1_inst[6:0]), .funct3(irom_1_inst_2[2:0]), .funct7(irom_1_inst_2[19:13]),
    .pc_sel(controller_1_pc_sel), .npc_op(controller_1_npc_op), .br_sel(controller_1_br_sel),
    .rf_we(controller_1_rf_we), .rf_wsel(controller_1_rf_wsel), .sext_op(controller_1_sext_op),
    .alu_op(controller_1_alu_op), .alub_sel(controller_1_alub_sel), .ram_we(controller_1_ram_we));
  RF rf_1 (
    .rR1(irom_1_inst_2[7:3]), .rR2(irom_1_inst_2[12:8]), .wR(irom_1_inst[11:7]), .we(controller_1_rf_we),
    .wD(multiplexer_2_out), .rD1(rf_1_rd1), .rD2(rf_1_rd2), .clk(clk), .rst(rst_btn));
  Multiplexer #(.select(1), .width(32), .disabled("Z"), .enable("false")) multiplexer_3 (
    .in0(rf_1_rd2), .in1(sext_1_ext), .out(multiplexer_3_out), .sel(controller_1_alub_sel));
  ALU alu_1 (.A(rf_1_rd1), .B(multiplexer_3_out), .C(alu_1_c), .zf(alu_1_zf), .sf(alu_1_sf), .op(controller_1_alu_op));
  Multiplexer #(.select(1), .width(1), .disabled("Z"), .enable("false")) multiplexer_4 (
    .in0(alu_1_zf), .in1(alu_1_sf), .out(multiplexer_4_out), .sel(controller_1_br_sel));
  DRAM dram_1 (.adr(alu_1_c), .we(controller_1_ram_we), .wdin(rf_1_rd2), .rdo(dram_1_rdo), .clk(clk));

  // Other names for the same wires on the sheet: rst = rst_btn

  // Notes on the sheet:
  //   rst_btn: pull=up
  //   ALU.f
  //   ALU.C
  //   EXT.ext
endmodule

module NPC (
  input  [31:0] PC,
  input  [31:0] offset,
  input  br,
  input  [1:0] op,
  output [31:0] npc,
  output [31:0] pc4,
  output [31:0] pcb
);
endmodule

module PC (
  input  rst,
  input  [31:0] din,
  input  clk,
  output [31:0] pc
);
endmodule

module IROM (
  input  [31:0] adr,
  output [31:0] inst
);
endmodule

module SEXT (
  input  [2:0] op,
  input  [19:0] din,
  output [31:0] ext
);
endmodule

module Controller (
  input  [6:0] opcode,
  input  [2:0] funct3,
  input  [6:0] funct7,
  output pc_sel,
  output [1:0] npc_op,
  output br_sel,
  output rf_we,
  output [2:0] rf_wsel,
  output [2:0] sext_op,
  output [3:0] alu_op,
  output alub_sel,
  output ram_we
);
endmodule

module RF (
  input  rst,
  input  [4:0] rR1,
  input  [4:0] rR2,
  input  [4:0] wR,
  input  we,
  input  [31:0] wD,
  input  clk,
  output [31:0] rD1,
  output [31:0] rD2
);
endmodule

module ALU (
  input  [3:0] op,
  input  [31:0] A,
  input  [31:0] B,
  output [31:0] C,
  output zf,
  output sf
);
endmodule

module DRAM (
  input  [31:0] adr,
  input  we,
  input  [31:0] wdin,
  input  clk,
  output [31:0] rdo
);
endmodule
