// Logisim project RISC-V_SoC.circ as structural Verilog: 13 circuits, main circuit SoC
module SoC (
);

  wire busmodel_1_ioen, busmodel_1_memr, busmodel_1_memw, clk, cpu_1_out_5, cpu_1_out_6, halt;
  wire [3:0] digitdriver_1_d0, digitdriver_1_d1, digitdriver_1_d2, digitdriver_1_d3, digitdriver_1_d4,
       digitdriver_1_d5, digitdriver_1_d6, digitdriver_1_d7;
  wire [11:0] busmodel_1_ioaddr12;
  wire [15:0] MissNumber;
  wire [23:0] leddriver_1_led0, undriven;
  wire [31:0] busmodel_1_iowritedata, busmodel_1_memaddr, busmodel_1_memwritedata, busmodel_1_readdata,
       cpu_1_out_16, cpu_1_out_17, cpu_1_out_18, dmem_1_read_data, Instruction, switchdriver_1_ioreaddata;

  Hex_Digit_Display hex_digit_display_1 (.value(digitdriver_1_d7));  // open: dp
  Hex_Digit_Display hex_digit_display_2 (.value(digitdriver_1_d6));  // open: dp
  Hex_Digit_Display hex_digit_display_3 (.value(digitdriver_1_d5));  // open: dp
  // Probe on cpu_1_out_16
  Clock #(.highDuration(1), .lowDuration(1)) clock_1 (.out(clk));
  Hex_Digit_Display hex_digit_display_4 (.value(digitdriver_1_d3));  // open: dp
  Hex_Digit_Display hex_digit_display_5 (.value(digitdriver_1_d4));  // open: dp
  Hex_Digit_Display hex_digit_display_6 (.value(digitdriver_1_d1));  // open: dp
  Hex_Digit_Display hex_digit_display_7 (.value(digitdriver_1_d2));  // open: dp
  DigitDriver digitdriver_1 (
    .in_1(clk), .IOEn(busmodel_1_ioen), .IOWriteData(busmodel_1_iowritedata), .IOAddr12(busmodel_1_ioaddr12),
    .D0(digitdriver_1_d0), .D4(digitdriver_1_d4), .D1(digitdriver_1_d1), .D5(digitdriver_1_d5),
    .D2(digitdriver_1_d2), .D6(digitdriver_1_d6), .D3(digitdriver_1_d3), .D7(digitdriver_1_d7));
  Hex_Digit_Display hex_digit_display_8 (.value(digitdriver_1_d0));  // open: dp
  IMEM imem_1 (.Instruction(Instruction), .Program_counter(cpu_1_out_16));
  // Probe on Instruction
  LED #(.active("true")) _23 (.in(leddriver_1_led0[23]));
  LED #(.active("true")) _19 (.in(leddriver_1_led0[19]));
  LED #(.active("true")) _20 (.in(leddriver_1_led0[20]));
  LED #(.active("true")) _21 (.in(leddriver_1_led0[21]));
  LED #(.active("true")) _22 (.in(leddriver_1_led0[22]));
  LED #(.active("true")) _15 (.in(leddriver_1_led0[15]));
  LED #(.active("true")) _16 (.in(leddriver_1_led0[16]));
  LED #(.active("true")) _17 (.in(leddriver_1_led0[17]));
  LED #(.active("true")) _18 (.in(leddriver_1_led0[18]));
  LEDDriver leddriver_1 (
    .in_1(clk), .IOEn(busmodel_1_ioen), .IOWriteData(busmodel_1_iowritedata), .IOAddr12(busmodel_1_ioaddr12),
    .LED0(leddriver_1_led0));
  LED #(.active("true")) _11 (.in(leddriver_1_led0[11]));
  LED #(.active("true")) _12 (.in(leddriver_1_led0[12]));
  LED #(.active("true")) _14 (.in(leddriver_1_led0[14]));
  LED #(.active("true")) _13 (.in(leddriver_1_led0[13]));
  LED #(.active("true")) _10 (.in(leddriver_1_led0[10]));
  LED #(.active("true")) _9 (.in(leddriver_1_led0[9]));
  LED #(.active("true")) _7 (.in(leddriver_1_led0[7]));
  LED #(.active("true")) _8 (.in(leddriver_1_led0[8]));
  cpu cpu_1 (
    .in_3(clk), .in_1(Instruction), .out_16(cpu_1_out_16), .out_17(cpu_1_out_17), .out_18(cpu_1_out_18),
    .out_5(cpu_1_out_5), .in_2(busmodel_1_readdata), .out_6(cpu_1_out_6), .out_7(halt));  // open: out_13, out_10, out_11, out_12, out_14, out_15, out_8, out_9, in_4
  LED #(.active("true")) _6 (.in(leddriver_1_led0[6]));
  LED #(.active("true")) _3 (.in(leddriver_1_led0[3]));
  LED #(.active("true")) _5 (.in(leddriver_1_led0[5]));
  LED #(.active("true")) _4 (.in(leddriver_1_led0[4]));
  LED #(.active("true")) _2 (.in(leddriver_1_led0[2]));
  LED #(.active("true")) _0 (.in(leddriver_1_led0[0]));
  LED #(.active("true")) _1 (.in(leddriver_1_led0[1]));
  BusModel busmodel_1 (
    .ReadData(busmodel_1_readdata), .IOAddr12(busmodel_1_ioaddr12), .IOEn(busmodel_1_ioen),
    .WriteData(cpu_1_out_18), .IOWriteData(busmodel_1_iowritedata), .MemRead(dmem_1_read_data),
    .IORead(switchdriver_1_ioreaddata), .R(cpu_1_out_5), .WriteAddr(cpu_1_out_17),
    .MemAddr(busmodel_1_memaddr), .MemR(busmodel_1_memr), .MemWriteData(busmodel_1_memwritedata),
    .W(cpu_1_out_6), .MemW(busmodel_1_memw));  // open: out_8
  // DipSwitch #(.NSwitches(24)) dipswitch_1: pin names not known; wires that end beside it: undriven[23], undriven[22], undriven[21], undriven[20], undriven[19], undriven[18], undriven[17], undriven[16], undriven[15], undriven[14], undriven[13], undriven[12]
  SwitchDriver switchdriver_1 (
    .in_1(clk), .SW0(undriven), .IOEn(busmodel_1_ioen), .IOAddr12(busmodel_1_ioaddr12),
    .IOReadData(switchdriver_1_ioreaddata));
  DMEM dmem_1 (
    .Write_En(busmodel_1_memw), .clk(clk), .Read_Data(dmem_1_read_data), .Address(busmodel_1_memaddr),
    .Write_Data(busmodel_1_memwritedata), .Read_En(busmodel_1_memr), .MissNubmer(MissNumber));

  // Notes on the sheet:
  //   DK7
  //   DK5
  //   DK6
  //   DK4
  //   DK3
  //   时钟
  //   DK2
  //   DK1
  //   DK0
  //   I/O总线
  //   20
  //   23
  //   22
  //   21
  //   17
  //   16
  //   18
  //   19
  //   12
  //   15
  //   13
  //   14
  //   9
  //   8
  //   11
  //   10
  //   7
  //   4
  //   5
  //   6
  //   1
  //   0
  //   2
  //   3
endmodule

module cpu (
  input  [31:0] in_1,
  input  [31:0] in_2,
  input  in_3,
  input  in_4,
  output out_5,
  output out_6,
  output out_7,
  output [31:0] out_8,
  output [31:0] out_9,
  output [31:0] out_10,
  output [31:0] out_11,
  output [31:0] out_12,
  output [31:0] out_13,
  output [31:0] out_14,
  output [31:0] out_15,
  output [31:0] out_16,
  output [31:0] out_17,
  output [31:0] out_18
);

  wire and_1_out, and_2_out, and_3_out, and_4_out, Branch, branch_1_breq, branch_1_brlt,
       controlmodel_1_alusela, controlmodel_1_aluselb, controlmodel_1_beq, controlmodel_1_bge,
       controlmodel_1_bgeu, controlmodel_1_blt, controlmodel_1_bltu, controlmodel_1_bne, controlmodel_1_brun,
       controlmodel_1_pcsel, controlmodel_1_regwrite, En, or_1_out, or_2_out;
  wire [1:0] controlmodel_1_wbsel;
  wire [2:0] controlmodel_1_immsel;
  wire [3:0] controlmodel_1_aluop;
  wire [31:0] adder_1_out, immmodel_1_immdiate, multiplexer_1_out, multiplexer_2_out, multiplexer_3_out,
       multiplexer_4_out, regfile_1_read_data_1;

  Adder #(.width(32)) adder_1 (.a(out_16), .b(32'h4), .out(adder_1_out));  // open: cin, cout
  Multiplexer #(.select(1), .width(32), .disabled("Z"), .enable("false")) multiplexer_1 (
    .in0(adder_1_out), .in1(out_17), .out(multiplexer_1_out), .sel(Branch));
  Register #(.width(32), .trigger("rising"), .Select("low")) PC (
    .D(multiplexer_1_out), .en(En), .Q(out_16), .clk(in_3));  // open: clr
  Comparator #(.width(32), .mode("unsigned")) comparator_1 (.a(in_1), .b({32{1'b0}}), .eq(out_7));  // open: gt, lt
  // Probe on adder_1_out
  // Probe on out_16
  nor nor_1 (En, out_7, in_4);
  Pull_Resistor #(.pull(0)) pull_resistor_1 (.node(in_4));
  // Probe on in_1
  ControlModel controlmodel_1 (
    .WBSel(controlmodel_1_wbsel), .Instruction(in_1), .BrUN(controlmodel_1_brun),
    .ALUSelB(controlmodel_1_aluselb), .ALUOP(controlmodel_1_aluop), .PCSel(controlmodel_1_pcsel),
    .ImmSel(controlmodel_1_immsel), .RegWrite(controlmodel_1_regwrite), .MemWrite(out_6),
    .ALUSelA(controlmodel_1_alusela), .MemRead(out_5), .BEQ(controlmodel_1_beq), .BNE(controlmodel_1_bne),
    .BGE(controlmodel_1_bge), .BLT(controlmodel_1_blt), .BLTU(controlmodel_1_bltu), .BGEU(controlmodel_1_bgeu));
  ImmModel immmodel_1 (.Immdiate(immmodel_1_immdiate), .INSTRUCTION(in_1), .InstructionType(controlmodel_1_immsel));
  RegFile regfile_1 (
    .rs1(in_1[19:15]), .rs2(in_1[24:20]), .rd(in_1[11:7]), .Write_Data(multiplexer_4_out),
    .RegWEn(controlmodel_1_regwrite), .clk(in_3), .Read_Data_1(regfile_1_read_data_1), .Read_Data_2(out_18),
    .ra(out_8), .sp(out_9), .t0(out_10), .t1(out_11), .t2(out_12), .s0(out_13), .s1(out_14), .a0(out_15));
  or or_1 (or_1_out, controlmodel_1_blt, controlmodel_1_bltu);
  or or_2 (or_2_out, controlmodel_1_bge, controlmodel_1_bgeu);
  Branch branch_1 (
    .BrEQ(branch_1_breq), .RS1(regfile_1_read_data_1), .RS2(out_18), .BrLT(branch_1_brlt),
    .BrUN(controlmodel_1_brun));
  Multiplexer #(.select(1), .width(32), .disabled("Z"), .enable("false")) multiplexer_2 (
    .in0(regfile_1_read_data_1), .in1(out_16), .out(multiplexer_2_out), .sel(controlmodel_1_alusela));
  Multiplexer #(.select(1), .width(32), .disabled("Z"), .enable("false")) multiplexer_3 (
    .in0(out_18), .in1(immmodel_1_immdiate), .out(multiplexer_3_out), .sel(controlmodel_1_aluselb));
  and and_1 (and_1_out, branch_1_breq, controlmodel_1_beq);
  and and_2 (and_2_out, ~branch_1_breq, controlmodel_1_bne);  // AND_Gate
  and and_3 (and_3_out, branch_1_brlt, or_1_out);
  and and_4 (and_4_out, ~branch_1_brlt, or_2_out);  // AND_Gate
  or or_3 (Branch, controlmodel_1_pcsel, and_1_out, and_2_out, and_3_out, and_4_out);
  // Probe on out_17
  AluModel alumodel_1 (.A(multiplexer_2_out), .Result(out_17), .B(multiplexer_3_out), .ALUSel(controlmodel_1_aluop));
  // Probe on out_18
  // Probe on in_2
  Multiplexer #(.select(2), .width(32), .disabled("Z"), .enable("false")) multiplexer_4 (
    .in0(adder_1_out), .in1(out_17), .in2(in_2), .out(multiplexer_4_out), .sel(controlmodel_1_wbsel));  // open: in3

  // Other names for the same wires on the sheet: a0[31:0] = out_15; clk = in_3; fetch_addr[31:0] = out_16;
  //   halt = out_7; Instruction[31:0] = in_1; MemR = out_5; MemW = out_6; Miss = in_4; ra[31:0] = out_8;
  //   ReadData[31:0] = in_2; s0[31:0] = out_13; s1[31:0] = out_14; sp[31:0] = out_9; t0[31:0] = out_10;
  //   t1[31:0] = out_11; t2[31:0] = out_12; WriteAddr[31:0] = out_17; WriteData[31:0] = out_18

  // Notes on the sheet:
  //   PC
  //   PC+4
  //   ALU_Result
  //   ALU_Result
  //   输入引脚区
  //   输出引脚区
  //   ALU_Result
  //   PC+4
  //   WriteData
  //   WBSel
endmodule

module RegFile (
  input  [4:0] rs1,
  input  [4:0] rs2,
  input  [4:0] rd,
  input  [31:0] Write_Data,
  input  RegWEn,
  input  clk,
  output [31:0] ra,
  output [31:0] sp,
  output [31:0] t0,
  output [31:0] t1,
  output [31:0] t2,
  output [31:0] s0,
  output [31:0] s1,
  output [31:0] a0,
  output [31:0] Read_Data_1,
  output [31:0] Read_Data_2
);

  wire write_en1, write_en2, write_en3, write_en4, write_en5, write_en6, write_en7, write_en8, write_en9,
       write_en10, write_en11, write_en12, write_en13, write_en14, write_en15, write_en16, write_en17,
       write_en18, write_en19, write_en20, write_en21, write_en22, write_en23, write_en24, write_en25,
       write_en26, write_en27, write_en28, write_en29, write_en30, write_en31;
  wire [31:0] x3, x4, x11, x12, x13, x14, x15, x16, x17, x18, x19, x20, x21, x22, x23, x24, x25, x26, x27,
       x28, x29, x30, x31;

  Pull_Resistor #(.pull(0)) pull_resistor_1 (.node(write_en1));
  Register #(.width(32), .trigger("rising"), .Select("low")) register_1 (
    .D(Write_Data), .en(write_en8), .Q(s0), .clk(clk));  // open: clr
  Register #(.width(32), .trigger("rising"), .Select("low")) register_2 (
    .D(Write_Data), .en(write_en16), .Q(x16), .clk(clk));  // open: clr
  Register #(.width(32), .trigger("rising"), .Select("low")) register_3 (
    .D(Write_Data), .en(write_en24), .Q(x24), .clk(clk));  // open: clr
  Pull_Resistor #(.pull(0)) pull_resistor_2 (.node(write_en2));
  Pull_Resistor #(.pull(0)) pull_resistor_3 (.node(write_en3));
  Pull_Resistor #(.pull(0)) pull_resistor_4 (.node(write_en4));
  Pull_Resistor #(.pull(0)) pull_resistor_5 (.node(write_en5));
  // Probe on ra
  Register #(.width(32), .trigger("rising"), .Select("low")) register_4 (
    .D(Write_Data), .en(write_en1), .Q(ra), .clk(clk));  // open: clr
  Register #(.width(32), .trigger("rising"), .Select("low")) register_5 (
    .D(Write_Data), .en(write_en9), .Q(s1), .clk(clk));  // open: clr
  Register #(.width(32), .trigger("rising"), .Select("low")) register_6 (
    .D(Write_Data), .en(write_en17), .Q(x17), .clk(clk));  // open: clr
  Register #(.width(32), .trigger("rising"), .Select("low")) register_7 (
    .D(Write_Data), .en(write_en25), .Q(x25), .clk(clk));  // open: clr
  Pull_Resistor #(.pull(0)) pull_resistor_6 (.node(write_en7));
  Pull_Resistor #(.pull(0)) pull_resistor_7 (.node(write_en6));
  Pull_Resistor #(.pull(0)) pull_resistor_8 (.node(write_en8));
  Pull_Resistor #(.pull(0)) pull_resistor_9 (.node(write_en9));
  // Probe on Write_Data
  // Probe on write_en18
  Pull_Resistor #(.pull(0)) pull_resistor_10 (.node(write_en10));
  Pull_Resistor #(.pull(0)) pull_resistor_11 (.node(write_en11));
  Register #(.width(32), .trigger("rising"), .Select("low")) register_8 (
    .D(Write_Data), .en(write_en2), .Q(sp), .clk(clk));  // open: clr
  Register #(.width(32), .trigger("rising"), .Select("low")) register_9 (
    .D(Write_Data), .en(write_en10), .Q(a0), .clk(clk));  // open: clr
  Register #(.width(32), .trigger("rising"), .Select("low")) register_10 (
    .D(Write_Data), .en(write_en18), .Q(x18), .clk(clk));  // open: clr
  // Probe on x18
  Register #(.width(32), .trigger("rising"), .Select("low")) register_11 (
    .D(Write_Data), .en(write_en26), .Q(x26), .clk(clk));  // open: clr
  Pull_Resistor #(.pull(0)) pull_resistor_12 (.node(write_en12));
  Pull_Resistor #(.pull(0)) pull_resistor_13 (.node(write_en13));
  Pull_Resistor #(.pull(0)) pull_resistor_14 (.node(write_en15));
  Pull_Resistor #(.pull(0)) pull_resistor_15 (.node(write_en14));
  Register #(.width(32), .trigger("rising"), .Select("low")) register_12 (
    .D(Write_Data), .en(write_en3), .Q(x3), .clk(clk));  // open: clr
  Register #(.width(32), .trigger("rising"), .Select("low")) register_13 (
    .D(Write_Data), .en(write_en11), .Q(x11), .clk(clk));  // open: clr
  Register #(.width(32), .trigger("rising"), .Select("low")) register_14 (
    .D(Write_Data), .en(write_en19), .Q(x19), .clk(clk));  // open: clr
  Register #(.width(32), .trigger("rising"), .Select("low")) register_15 (
    .D(Write_Data), .en(write_en27), .Q(x27), .clk(clk));  // open: clr
  Pull_Resistor #(.pull(0)) pull_resistor_16 (.node(write_en16));
  Pull_Resistor #(.pull(0)) pull_resistor_17 (.node(write_en17));
  Pull_Resistor #(.pull(0)) pull_resistor_18 (.node(write_en18));
  Pull_Resistor #(.pull(0)) pull_resistor_19 (.node(write_en19));
  Register #(.width(32), .trigger("rising"), .Select("low")) register_16 (
    .D(Write_Data), .en(write_en4), .Q(x4), .clk(clk));  // open: clr
  Register #(.width(32), .trigger("rising"), .Select("low")) register_17 (
    .D(Write_Data), .en(write_en12), .Q(x12), .clk(clk));  // open: clr
  Register #(.width(32), .trigger("rising"), .Select("low")) register_18 (
    .D(Write_Data), .en(write_en20), .Q(x20), .clk(clk));  // open: clr
  Register #(.width(32), .trigger("rising"), .Select("low")) register_19 (
    .D(Write_Data), .en(write_en28), .Q(x28), .clk(clk));  // open: clr
  Pull_Resistor #(.pull(0)) pull_resistor_20 (.node(write_en20));
  Pull_Resistor #(.pull(0)) pull_resistor_21 (.node(write_en21));
  Pull_Resistor #(.pull(0)) pull_resistor_22 (.node(write_en23));
  Pull_Resistor #(.pull(0)) pull_resistor_23 (.node(write_en22));
  Decoder #(.select(5), .tristate("false"), .disabled("Z"), .enable("true")) decoder_1 (
    .out1(write_en1), .out2(write_en2), .out3(write_en3), .out4(write_en4), .out5(write_en5),
    .out6(write_en6), .out7(write_en7), .out8(write_en8), .out9(write_en9), .out10(write_en10),
    .out11(write_en11), .out12(write_en12), .out13(write_en13), .out14(write_en14), .out15(write_en15),
    .out16(write_en16), .out17(write_en17), .out18(write_en18), .out19(write_en19), .out20(write_en20),
    .out21(write_en21), .out22(write_en22), .out23(write_en23), .out24(write_en24), .out25(write_en25),
    .out26(write_en26), .out27(write_en27), .out28(write_en28), .out29(write_en29), .out30(write_en30),
    .out31(write_en31), .sel(rd), .en(RegWEn));  // open: out0
  Register #(.width(32), .trigger("rising"), .Select("low")) register_20 (
    .D(Write_Data), .en(write_en5), .Q(t0), .clk(clk));  // open: clr
  Register #(.width(32), .trigger("rising"), .Select("low")) register_21 (
    .D(Write_Data), .en(write_en13), .Q(x13), .clk(clk));  // open: clr
  Register #(.width(32), .trigger("rising"), .Select("low")) register_22 (
    .D(Write_Data), .en(write_en21), .Q(x21), .clk(clk));  // open: clr
  Register #(.width(32), .trigger("rising"), .Select("low")) register_23 (
    .D(Write_Data), .en(write_en29), .Q(x29), .clk(clk));  // open: clr
  Pull_Resistor #(.pull(0)) pull_resistor_24 (.node(write_en24));
  // Probe on rd
  Pull_Resistor #(.pull(0)) pull_resistor_25 (.node(write_en25));
  Pull_Resistor #(.pull(0)) pull_resistor_26 (.node(write_en26));
  Pull_Resistor #(.pull(0)) pull_resistor_27 (.node(write_en27));
  Pull_Resistor #(.pull(0)) pull_resistor_28 (.node(write_en28));
  Register #(.width(32), .trigger("rising"), .Select("low")) register_24 (
    .D(Write_Data), .en(write_en6), .Q(t1), .clk(clk));  // open: clr
  Register #(.width(32), .trigger("rising"), .Select("low")) register_25 (
    .D(Write_Data), .en(write_en14), .Q(x14), .clk(clk));  // open: clr
  Register #(.width(32), .trigger("rising"), .Select("low")) register_26 (
    .D(Write_Data), .en(write_en22), .Q(x22), .clk(clk));  // open: clr
  Register #(.width(32), .trigger("rising"), .Select("low")) register_27 (
    .D(Write_Data), .en(write_en30), .Q(x30), .clk(clk));  // open: clr
  // Probe on x30
  Pull_Resistor #(.pull(0)) pull_resistor_29 (.node(write_en29));
  Pull_Resistor #(.pull(0)) pull_resistor_30 (.node(write_en31));
  Pull_Resistor #(.pull(0)) pull_resistor_31 (.node(write_en30));
  // Probe on Read_Data_1
  // Probe on rs1
  Register #(.width(32), .trigger("rising"), .Select("low")) register_28 (
    .D(Write_Data), .en(write_en7), .Q(t2), .clk(clk));  // open: clr
  Register #(.width(32), .trigger("rising"), .Select("low")) register_29 (
    .D(Write_Data), .en(write_en15), .Q(x15), .clk(clk));  // open: clr
  Register #(.width(32), .trigger("rising"), .Select("low")) register_30 (
    .D(Write_Data), .en(write_en23), .Q(x23), .clk(clk));  // open: clr
  Register #(.width(32), .trigger("rising"), .Select("low")) register_31 (
    .D(Write_Data), .en(write_en31), .Q(x31), .clk(clk));  // open: clr
  Multiplexer #(.select(5), .width(32), .disabled("Z"), .enable("false")) multiplexer_1 (
    .in0({32{1'b0}}), .in1(ra), .in2(sp), .in3(x3), .in4(x4), .in5(t0), .in6(t1), .in7(t2), .in8(s0),
    .in9(s1), .in10(a0), .in11(x11), .in12(x12), .in13(x13), .in14(x14), .in15(x15), .in16(x16), .in17(x17),
    .in18(x18), .in19(x19), .in20(x20), .in21(x21), .in22(x22), .in23(x23), .in24(x24), .in25(x25),
    .in26(x26), .in27(x27), .in28(x28), .in29(x29), .in30(x30), .in31(x31), .out(Read_Data_1), .sel(rs1));
  // Probe on Read_Data_2
  // Probe on rs2
  Multiplexer #(.select(5), .width(32), .disabled("Z"), .enable("false")) multiplexer_2 (
    .in0({32{1'b0}}), .in1(ra), .in2(sp), .in3(x3), .in4(x4), .in5(t0), .in6(t1), .in7(t2), .in8(s0),
    .in9(s1), .in10(a0), .in11(x11), .in12(x12), .in13(x13), .in14(x14), .in15(x15), .in16(x16), .in17(x17),
    .in18(x18), .in19(x19), .in20(x20), .in21(x21), .in22(x22), .in23(x23), .in24(x24), .in25(x25),
    .in26(x26), .in27(x27), .in28(x28), .in29(x29), .in30(x30), .in31(x31), .out(Read_Data_2), .sel(rs2));

  // Other names for the same wires on the sheet: read_data1[31:0] = Read_Data_1; read_data2[31:0] = Read_Data_2;
  //   read_reg1[4:0] = rs1; read_reg2[4:0] = rs2; write_en = RegWEn; write_reg[4:0] = rd; x1[31:0] = ra;
  //   x2[31:0] = sp; x5[31:0] = t0; x6[31:0] = t1; x7[31:0] = t2; x8[31:0] = s0; x9[31:0] = s1; x10[31:0] = a0

  // Notes on the sheet:
  //   INPUTS to your circuit
  //   DON'T CHANGE THE LOCATIONS OF THE INPUTS AND OUTPUTS!
  //   These are DEBUG/TEST outputs from your circuit.
  //   OUTPUTS from your circuit
endmodule

module ControlModel (
  input  [31:0] Instruction,
  output BrUN,
  output RegWrite,
  output MemWrite,
  output MemRead,
  output PCSel,
  output [2:0] ImmSel,
  output ALUSelA,
  output ALUSelB,
  output [1:0] WBSel,
  output [3:0] ALUOP,
  output BEQ,
  output BLT,
  output BNE,
  output BLTU,
  output BGE,
  output BGEU
);

  wire and_5_out, and_10_out, comparator_3_eq, comparator_4_eq, comparator_5_eq, comparator_6_eq,
       comparator_7_eq, comparator_8_eq, comparator_13_eq, comparator_14_eq, comparator_15_eq,
       comparator_16_eq, comparator_17_eq, comparator_18_eq, comparator_19_eq, comparator_20_eq, IType, JALR,
       Load, or_2_out, or_3_out, or_4_out, or_5_out, or_11_out, or_12_out, RType, SBType, UJType, UType;
  wire [1:0] priority_encoder_4_out;
  wire [2:0] priority_encoder_3_out;
  wire [3:0] AOP_I, AOP_R, rom_2_data;

  Comparator #(.width(7), .mode("unsigned")) comparator_1 (
    .a(Instruction[6:0]), .b(7'b0110011), .eq(RType));  // open: gt, lt
  Comparator #(.width(7), .mode("unsigned")) comparator_2 (
    .a(Instruction[6:0]), .b(7'b0000011), .eq(MemRead));  // open: gt, lt
  Comparator #(.width(7), .mode("unsigned")) comparator_3 (
    .a(Instruction[6:0]), .b(7'b1100111), .eq(comparator_3_eq));  // open: gt, lt
  Comparator #(.width(7), .mode("unsigned")) comparator_4 (
    .a(Instruction[6:0]), .b(7'b0010011), .eq(comparator_4_eq));  // open: gt, lt
  Comparator #(.width(7), .mode("unsigned")) comparator_5 (
    .a(Instruction[6:0]), .b(7'b0000011), .eq(comparator_5_eq));  // open: gt, lt
  and and_1 (Load, comparator_5_eq, IType);
  Comparator #(.width(3), .mode("unsigned")) comparator_6 (
    .a(Instruction[14:12]), .b(3'b000), .eq(comparator_6_eq));  // open: gt, lt
  Comparator #(.width(3), .mode("unsigned")) comparator_7 (
    .a(Instruction[14:12]), .b(3'b001), .eq(comparator_7_eq));  // open: gt, lt
  Comparator #(.width(3), .mode("unsigned")) comparator_8 (
    .a(Instruction[14:12]), .b(3'b101), .eq(comparator_8_eq));  // open: gt, lt
  or or_1 (IType, MemRead, comparator_3_eq, comparator_4_eq);
  and and_2 (BEQ, comparator_6_eq, SBType);
  and and_3 (BNE, comparator_7_eq, SBType);
  and and_4 (BGE, comparator_8_eq, SBType);
  and and_5 (and_5_out, IType, ~JALR);  // AND_Gate
  Comparator #(.width(7), .mode("unsigned")) comparator_9 (
    .a(Instruction[6:0]), .b(7'b0110111), .eq(UType));  // open: gt, lt
  Comparator #(.width(7), .mode("unsigned")) comparator_10 (
    .a(Instruction[6:0]), .b(7'b1101111), .eq(UJType));  // open: gt, lt
  Comparator #(.width(7), .mode("unsigned")) comparator_11 (
    .a(Instruction[6:0]), .b(7'b0100011), .eq(MemWrite));  // open: gt, lt
  Comparator #(.width(7), .mode("unsigned")) comparator_12 (
    .a(Instruction[6:0]), .b(7'b1100011), .eq(SBType));  // open: gt, lt
  Comparator #(.width(7), .mode("unsigned")) comparator_13 (
    .a(Instruction[6:0]), .b(7'b1100111), .eq(comparator_13_eq));  // open: gt, lt
  Comparator #(.width(3), .mode("unsigned")) comparator_14 (
    .a(Instruction[14:12]), .b(3'b100), .eq(comparator_14_eq));  // open: gt, lt
  Comparator #(.width(3), .mode("unsigned")) comparator_15 (
    .a(Instruction[14:12]), .b(3'b110), .eq(comparator_15_eq));  // open: gt, lt
  Comparator #(.width(3), .mode("unsigned")) comparator_16 (
    .a(Instruction[14:12]), .b(3'b111), .eq(comparator_16_eq));  // open: gt, lt
  and and_6 (JALR, comparator_13_eq, IType);
  or or_2 (or_2_out, RType, and_5_out, UType);
  and and_7 (BLT, comparator_14_eq, SBType);
  and and_8 (BLTU, comparator_15_eq, SBType);
  and and_9 (BGEU, comparator_16_eq, SBType);
  or or_3 (or_3_out, UJType, JALR);
  or or_4 (or_4_out, or_3_out, or_2_out, Load);
  Priority_Encoder #(.select(3), .disabled("Z")) priority_encoder_1 (
    .in0(IType), .in1(MemWrite), .in2(SBType), .in3(UType), .in4(UJType), .out(ImmSel), .en_in(or_5_out));  // open: in5, in6, in7, gs, en_out
  or or_5 (or_5_out, IType, MemWrite, SBType, UType, UJType);
  Priority_Encoder #(.select(2), .disabled("Z")) priority_encoder_2 (
    .in0(or_3_out), .in1(or_2_out), .in2(Load), .out(WBSel), .en_in(or_4_out));  // open: in3, gs, en_out
  Pull_Resistor #(.pull(0)) pull_resistor_1 (.node(WBSel));
  or or_6 (BrUN, BLTU, BGEU);
  or or_7 (RegWrite, RType, IType, UType, UJType);
  or or_8 (PCSel, JALR, UJType);
  Pull_Resistor #(.pull(0)) pull_resistor_2 (.node(ImmSel));
  or or_9 (ALUSelA, SBType, UJType);
  or or_10 (ALUSelB, IType, MemWrite, SBType, UType, UJType);
  // Probe on PCSel
  // Probe on Instruction[6:0]
  Comparator #(.width(7), .mode("unsigned")) comparator_17 (
    .a(7'b0010011), .b(Instruction[6:0]), .eq(comparator_17_eq));  // open: gt, lt
  Comparator #(.width(3), .mode("unsigned")) comparator_18 (
    .a(3'b101), .b(Instruction[14:12]), .eq(comparator_18_eq));  // open: gt, lt
  Comparator #(.width(7), .mode("unsigned")) comparator_19 (
    .a(7'b0100000), .b(Instruction[31:25]), .eq(comparator_19_eq));  // open: gt, lt
  Comparator #(.width(7), .mode("unsigned")) comparator_20 (
    .a(7'b0000011), .b(Instruction[6:0]), .eq(comparator_20_eq));  // open: gt, lt
  // Probe on comparator_20_eq
  ROM #(.addrWidth(10), .dataWidth(4), .Select("high")) rom_1 (
    .addr({Instruction[14:12], Instruction[31:25]}), .data(AOP_R));
  ROM #(.addrWidth(3), .dataWidth(4), .Select("high")) rom_2 (.addr(Instruction[14:12]), .data(rom_2_data));
  // Probe on and_10_out
  and and_10 (and_10_out, comparator_17_eq, comparator_18_eq, comparator_19_eq);
  or or_11 (or_11_out, and_10_out, comparator_20_eq);
  Priority_Encoder #(.select(3), .disabled("Z")) priority_encoder_3 (
    .in0(RType), .in1(IType), .in2(MemWrite), .in3(SBType), .in4(UType), .in5(UJType),
    .out(priority_encoder_3_out), .en_in(or_12_out));  // open: in6, in7, gs, en_out
  or or_12 (or_12_out, RType, IType, MemWrite, SBType, UType, UJType);
  Priority_Encoder #(.select(2), .disabled("Z")) priority_encoder_4 (
    .in1(and_10_out), .in2(comparator_20_eq), .out(priority_encoder_4_out), .en_in(or_11_out));  // open: in0, in3, gs, en_out
  // Probe on or_11_out
  Pull_Resistor #(.pull(0)) pull_resistor_3 (.node(priority_encoder_3_out));
  // Probe on AOP_I
  Multiplexer #(.select(2), .width(4), .disabled("Z"), .enable("false")) multiplexer_1 (
    .in0(rom_2_data), .in1(4'b0101), .in2(4'b0000), .out(AOP_I), .sel(priority_encoder_4_out));  // open: in3
  Pull_Resistor #(.pull(0)) pull_resistor_4 (.node(priority_encoder_4_out));
  // Probe on priority_encoder_3_out
  // Probe on priority_encoder_4_out
  Multiplexer #(.select(3), .width(4), .disabled("Z"), .enable("false")) multiplexer_2 (
    .in0(AOP_R), .in1(AOP_I), .in2(4'b0000), .in3(4'b0000), .in4(4'b1101), .in5(4'b0000), .out(ALUOP),
    .sel(priority_encoder_3_out));  // open: in6, in7
  // Probe on ALUOP

  // Other names for the same wires on the sheet: Funct7[6:0] = Instruction[31:25]; Funct3[2:0] = Instruction[14:12];
  //   AOP[3:0] = ALUOP; OPCODE[6:0] = Instruction[6:0]; SType = MemWrite

  // Notes on the sheet:
  //   Extract the filed in Instrutions
  //   contents of rom_1 (hex, n*v repeats v):
  //   0 a c 12*0 f 16*0 c 95*0 6 e 126*0 7 128*0 b 126*0 3 127*0 4 8 30*0 5 95*0 2 127*0 1 9
  //   contents of rom_2 (hex, n*v repeats v):
  //   0 6 7 7 3 4 2 1
endmodule

module AluModel (
  input  [31:0] A,
  input  [31:0] B,
  input  [3:0] ALUSel,
  output [31:0] Result
);

  wire adder_3_cout, bitselector_1_out, bitselector_2_out, xor_1_out;
  wire [0:0] slt_alu;
  wire [15:0] adder_5_out, undriven, undriven_2;
  wire [31:0] add, adder_1_out, adder_3_out, and_alu, divu_alu, mul_alu, mulh_alu, mulhu_alu,
       multiplexer_1_out, multiplexer_2_out, multiplier_1_cout, multiplier_1_out, negator_1_out,
       negator_2_out, not_1_out, not_2_out, or_alu, remu_alu, sll_alu, sra_alu, srl_alu, sub_alu, xor_alu;
  wire [31:16] vaddh_alu;

  BitSelector #(.width(32), .group(1)) bitselector_1 (.in(A), .out(bitselector_1_out), .sel({5{1'b1}}));
  BitSelector #(.width(32), .group(1)) bitselector_2 (.in(B), .out(bitselector_2_out), .sel({5{1'b1}}));
  Negator #(.width(32)) negator_1 (.in(A), .out(negator_1_out));
  Negator #(.width(32)) negator_2 (.in(B), .out(negator_2_out));
  Multiplexer #(.select(1), .width(32), .disabled("Z"), .enable("false")) multiplexer_1 (
    .in0(A), .in1(negator_1_out), .out(multiplexer_1_out), .sel(bitselector_1_out));
  Multiplexer #(.select(1), .width(32), .disabled("Z"), .enable("false")) multiplexer_2 (
    .in0(B), .in1(negator_2_out), .out(multiplexer_2_out), .sel(bitselector_2_out));
  Multiplier #(.width(32)) multiplier_1 (
    .a(multiplexer_1_out), .b(multiplexer_2_out), .out(multiplier_1_out), .cout(multiplier_1_cout));  // open: cin
  xor xor_1 (xor_1_out, bitselector_1_out, bitselector_2_out);
  assign not_1_out = ~multiplier_1_out;  // NOT_Gate not_1, 32 bits wide
  Adder #(.width(32)) adder_1 (.a({32{1'b0}}), .b(not_2_out), .out(adder_1_out), .cin(adder_3_cout));  // open: cout
  assign not_2_out = ~multiplier_1_cout;  // NOT_Gate not_2, 32 bits wide
  Adder #(.width(32)) adder_2 (.a(A), .b(B), .out(add));  // open: cin, cout
  assign and_alu = A & B;  // AND_Gate and_1, 32 bits wide
  assign or_alu = A | B;  // OR_Gate or_1, 32 bits wide
  assign xor_alu = A ^ B;  // XOR_Gate xor_2, 32 bits wide
  Shifter #(.width(32), .shift("lr")) shifter_1 (.in(A), .\dist (B[4:0]), .out(srl_alu));
  Shifter #(.width(32), .shift("ar")) shifter_2 (.in(A), .\dist (B[4:0]), .out(sra_alu));
  Shifter #(.width(32), .shift("ll")) shifter_3 (.in(A), .\dist (B[4:0]), .out(sll_alu));
  Comparator #(.width(32), .mode("twosComplement")) comparator_1 (.a(A), .b(B), .lt(slt_alu[0]));  // open: gt, eq
  Adder #(.width(32)) adder_3 (.a(32'h1), .b(not_1_out), .out(adder_3_out), .cout(adder_3_cout));  // open: cin
  Multiplexer #(.select(1), .width(32), .disabled("Z"), .enable("false")) multiplexer_3 (
    .in0(multiplier_1_out), .in1(adder_3_out), .out(mul_alu), .sel(xor_1_out));
  Multiplexer #(.select(1), .width(32), .disabled("Z"), .enable("false")) multiplexer_4 (
    .in0(multiplier_1_cout), .in1(adder_1_out), .out(mulh_alu), .sel(xor_1_out));
  Divider #(.width(32)) divider_1 (.a(A), .b(B), .out(divu_alu), .rem(remu_alu));  // open: upper
  Multiplier #(.width(32)) multiplier_2 (.a(A), .b(B), .cout(mulhu_alu));  // open: out, cin
  Subtractor #(.width(32)) subtractor_1 (.a(A), .b(B), .out(sub_alu));  // open: bin, bout
  // Probe on Result
  Multiplexer #(.select(4), .width(32), .disabled("Z"), .enable("false")) multiplexer_5 (
    .in0(add), .in1(and_alu), .in2(or_alu), .in3(xor_alu), .in4(srl_alu), .in5(sra_alu), .in6(sll_alu),
    .in7({{31{1'b0}}, slt_alu[0]}), .in8(divu_alu), .in9(remu_alu), .in10(mul_alu), .in11(mulhu_alu),
    .in12(sub_alu), .in13(B), .in14(mulh_alu), .in15({vaddh_alu, vaddh_alu}), .out(Result), .sel(ALUSel));
  Adder #(.width(16)) adder_4 (.a(A[31:16]), .b(B[31:16]), .out(vaddh_alu));  // open: cin, cout
  Adder #(.width(16)) adder_5 (.a(undriven), .b(undriven_2), .out(adder_5_out));  // open: cin, cout

  // Other names for the same wires on the sheet: vaddh_alu[15:0] = vaddh_alu

  // Notes on the sheet:
  //   INPUTS to your circuit
  //   DON'T CHANGE THE LOCATIONS OF THE INPUTS AND OUTPUTS!
  //   OUTPUT from your circuit
endmodule

module ImmModel (
  input  [31:0] INSTRUCTION,
  input  [2:0] InstructionType,
  output [31:0] Immdiate
);

  wire [31:0] bit_extender_1_out, bit_extender_2_out, bit_extender_3_out, bit_extender_4_out;

  // Probe on INSTRUCTION
  assign bit_extender_1_out = {{20{INSTRUCTION[31]}}, INSTRUCTION[31:20]};  // Bit_Extender bit_extender_1
  assign bit_extender_2_out = {{20{INSTRUCTION[31]}}, {INSTRUCTION[31:25], INSTRUCTION[11:7]}};  // Bit_Extender bit_extender_2
  assign bit_extender_3_out = {{19{INSTRUCTION[31]}}, {INSTRUCTION[31], INSTRUCTION[7], INSTRUCTION[30:25], INSTRUCTION[11:8], 1'b0}};  // Bit_Extender bit_extender_3
  // Probe on bit_extender_3_out
  assign bit_extender_4_out = {{11{INSTRUCTION[31]}}, {INSTRUCTION[31], INSTRUCTION[19:12], INSTRUCTION[20], INSTRUCTION[30:21], 1'b0}};  // Bit_Extender bit_extender_4
  Multiplexer #(.select(3), .width(32), .disabled("Z"), .enable("false")) multiplexer_1 (
    .in0(bit_extender_1_out), .in1(bit_extender_2_out), .in2(bit_extender_3_out),
    .in3({INSTRUCTION[31:12], {12{1'b0}}}), .in4(bit_extender_4_out), .out(Immdiate), .sel(InstructionType));  // open: in5, in6, in7

  // Notes on the sheet:
  //   I
  //   S
  //   U
  //   SB
  //   UJ
endmodule

module Branch (
  input  [31:0] RS1,
  input  [31:0] RS2,
  input  BrUN,
  output BrEQ,
  output BrLT
);

  wire comparator_1_lt, comparator_2_lt;

  Comparator #(.width(32), .mode("twosComplement")) comparator_1 (
    .a(RS1), .b(RS2), .eq(BrEQ), .lt(comparator_1_lt));  // open: gt
  Comparator #(.width(32), .mode("unsigned")) comparator_2 (.a(RS1), .b(RS2), .lt(comparator_2_lt));  // open: gt, eq
  Multiplexer #(.select(1), .width(1), .disabled("Z"), .enable("false")) multiplexer_1 (
    .in0(comparator_1_lt), .in1(comparator_2_lt), .out(BrLT), .sel(BrUN));
endmodule

module IMEM (
  input  [31:0] Program_counter,
  output [31:0] Instruction
);

  ROM #(.addrWidth(16), .dataWidth(32), .Select("high")) rom_1 (.addr(Program_counter[17:2]), .data(Instruction));

  // Notes on the sheet:
  //   contents of rom_1 (hex, n*v repeats v):
  //   fffff4b7 40006f c000ef 10000ef 740006f 704a403 8067 1545693 76f693 845593 ff5f593 ff47613 8067 293
  //   800313 393 2628063 555e33 1e7e13 229e93 1de1e33 1c3e3b3 128293 fe5ff06f 74a023 1a40006f 8057f93
  //   7f57293 f8663 4f9f93 1f2e2b3 54a023 1880006f 2068c63 100293 2568c63 200293 2568c63 300293 2568c63
  //   400293 4568263 500293 4568863 600293 6568463 1500006f c5f533 f75ff06f c5e533 f6dff06f c5c533
  //   f65ff06f 805ff93 7f5f513 c51533 1f56533 f85ff06f 805ff93 7f5f513 40c55533 1f56533 f71ff06f 66533
  //   f2058ae3 8057f93 f20f86e3 7f57513 fff54513 150513 f1dff06f 6513 f40604e3 c5cfb3 80fff93 7f5f313
  //   7f67393 f2734ae3 4000f13 1e35863 131313 139393 ff5ff06f 6293 1e3d863 139393 128293 ff5ff06f 202c463
  //   40730333 151513 34663 156513 80006f 730333 13d393 fff28293 fddff06f 1f56533 eddff06f 6513 ec060ae3
  //   c5cfb3 80fff93 7f5f313 7f67393 fff3ce13 1e0e13 293 600e93 1c30333 8037f13 ea0f14e3 3d28863 8037f13
  //   7f5f13 1e56533 131313 151513 f0663 730333 80006f 1c30333 128293 fd5ff06f 8037f13 7f5f13 1e56533
  //   1f56533 e65ff06f e01ff06f
endmodule

module DMEM (
  input  [31:0] Write_Data,
  input  clk,
  input  Read_En,
  input  [31:0] Address,
  input  Write_En,
  output [15:0] MissNubmer,
  output [31:0] Read_Data
);

  wire and_1_out, and_2_out, and_3_out, and_4_out, is_MemAddr, is_RomAddr, or_1_out;
  wire [15:0] controlled_buffer_3_out;
  wire [31:0] controlled_buffer_1_out, controlled_buffer_2_out, ram_1_data, rom_1_data;

  or or_1 (or_1_out, Read_En, Write_En);
  and and_1 (and_1_out, or_1_out, is_MemAddr);
  assign controlled_buffer_1_out = and_1_out ? Address : 32'bz;  // Controlled_Buffer controlled_buffer_1
  Comparator #(.width(4), .mode("unsigned")) comparator_1 (
    .a(Address[31:28]), .b(4'b1000), .eq(is_RomAddr));  // open: gt, lt
  assign controlled_buffer_2_out = and_2_out ? Write_Data : 32'bz;  // Controlled_Buffer controlled_buffer_2
  and and_2 (and_2_out, is_MemAddr, Write_En);
  assign controlled_buffer_3_out = is_RomAddr ? Address[17:2] : 16'bz;  // Controlled_Buffer controlled_buffer_3
  not not_1 (is_MemAddr, is_RomAddr);
  RAM #(.addrWidth(16), .dataWidth(32), .bus("separate"), .Select("high")) ram_1 (
    .addr(controlled_buffer_1_out[17:2]), .din(controlled_buffer_2_out), .data(ram_1_data), .str(and_2_out),
    .clk(clk), .ld(1'b1));  // open: sel, clr
  ROM #(.addrWidth(16), .dataWidth(32), .Select("high")) rom_1 (.addr(controlled_buffer_3_out), .data(rom_1_data));
  and and_3 (and_3_out, Read_En, is_MemAddr);
  assign Read_Data = and_3_out ? ram_1_data : 32'bz;  // Controlled_Buffer controlled_buffer_4
  assign Read_Data = and_4_out ? rom_1_data : 32'bz;  // Controlled_Buffer controlled_buffer_5
  and and_4 (and_4_out, Read_En, is_RomAddr);

  // Other names for the same wires on the sheet: Addr[31:0] = Address; MissNumber[15:0] = MissNubmer;
  //   ReadData[31:0] = Read_Data; ReadEnable = Read_En; WriteData[31:0] = Write_Data; WriteEnable = Write_En

  // Notes on the sheet:
  //   输入引脚区
  //   RAM
  //   二级存储器 ROM
  //   contents of rom_1 (hex, n*v repeats v):
  //   0 1 2 3 4 5 6 7 8 9 a b c d e f 10 11 12 13 14 15 16 17 18 19 1a 1b 1c 1d 1e 1f 20 21 22 23 24 25 26
  //   27 28 29 2a 2b 2c 2d 2e 2f 30 31 32 33 34 35 36 37 38 39 3a 3b 3c 3d 3e 3f 40 41 42 43 44 45 46 47
  //   48 49 4a 4b 4c 4d 4e 4f 50 51 52 53 54 55 56 57 58 59 5a 5b 5c 5d 5e 5f 60 61 62 63 64 65 66 67 68
  //   69 6a 6b 6c 6d 6e 6f 70 71 72 73 74 75 76 77 78 79 7a 7b 7c 7d 7e 7f ffffff80 ffffff81 ffffff82
  //   ffffff83 ffffff84 ffffff85 ffffff86 ffffff87 ffffff88 ffffff89 ffffff8a ffffff8b ffffff8c ffffff8d
  //   ffffff8e ffffff8f ffffff90 ffffff91 ffffff92 ffffff93 ffffff94 ffffff95 ffffff96 ffffff97 ffffff98
  //   ffffff99 ffffff9a ffffff9b ffffff9c ffffff9d ffffff9e ffffff9f ffffffa0 ffffffa1 ffffffa2 ffffffa3
  //   ffffffa4 ffffffa5 ffffffa6 ffffffa7 ffffffa8 ffffffa9 ffffffaa ffffffab ffffffac ffffffad ffffffae
  //   ffffffaf ffffffb0 ffffffb1 ffffffb2 ffffffb3 ffffffb4 ffffffb5 ffffffb6 ffffffb7 ffffffb8 ffffffb9
  //   ffffffba ffffffbb ffffffbc ffffffbd ffffffbe ffffffbf ffffffc0 ffffffc1 ffffffc2 ffffffc3 ffffffc4
  //   ffffffc5 ffffffc6 ffffffc7 ffffffc8 ffffffc9 ffffffca ffffffcb ffffffcc ffffffcd ffffffce ffffffcf
  //   ffffffd0 ffffffd1 ffffffd2 ffffffd3 ffffffd4 ffffffd5 ffffffd6 ffffffd7 ffffffd8 ffffffd9 ffffffda
  //   ffffffdb ffffffdc ffffffdd ffffffde ffffffdf ffffffe0 ffffffe1 ffffffe2 ffffffe3 ffffffe4 ffffffe5
  //   ffffffe6 ffffffe7 ffffffe8 ffffffe9 ffffffea ffffffeb ffffffec ffffffed ffffffee ffffffef fffffff0
  //   fffffff1 fffffff2 fffffff3 fffffff4 fffffff5 fffffff6 fffffff7 fffffff8 fffffff9 fffffffa fffffffb
  //   fffffffc fffffffd fffffffe ffffffff 0 1 2 3 4 5 6 7 8 9 a b c d e f 10 11 12 13 14 15 16 17 18 19 1a
  //   1b 1c 1d 1e 1f 20 21 22 23 24 25 26 27 28 29 2a 2b 2c 2d 2e 2f 30 31 32 33 34 35 36 37 38 39 3a 3b
  //   3c 3d 3e 3f 40 41 42 43 44 45 46 47 48 49 4a 4b 4c 4d 4e 4f 50 51 52 53 54 55 56 57 58 59 5a 5b 5c
  //   5d 5e 5f 60 61 62 63 64 65 66 67 68 69 6a 6b 6c 6d 6e 6f 70 71 72 73 74 75 76 77 78 79 7a 7b 7c 7d
  //   7e 7f ffffff80 ffffff81 ffffff82 ffffff83 ffffff84 ffffff85 ffffff86 ffffff87 ffffff88 ffffff89
  //   ffffff8a ffffff8b ffffff8c ffffff8d ffffff8e ffffff8f ffffff90 ffffff91 ffffff92 ffffff93 ffffff94
  //   ffffff95 ffffff96 ffffff97 ffffff98 ffffff99 ffffff9a ffffff9b ffffff9c ffffff9d ffffff9e ffffff9f
  //   ffffffa0 ffffffa1 ffffffa2 ffffffa3 ffffffa4 ffffffa5 ffffffa6 ffffffa7 ffffffa8 ffffffa9 ffffffaa
  //   ffffffab ffffffac ffffffad ffffffae ffffffaf ffffffb0 ffffffb1 ffffffb2 ffffffb3 ffffffb4 ffffffb5
  //   ffffffb6 ffffffb7 ffffffb8 ffffffb9 ffffffba ffffffbb ffffffbc ffffffbd ffffffbe ffffffbf ffffffc0
  //   ffffffc1 ffffffc2 ffffffc3 ffffffc4 ffffffc5 ffffffc6 ffffffc7 ffffffc8 ffffffc9 ffffffca ffffffcb
  //   ffffffcc ffffffcd ffffffce ffffffcf ffffffd0 ffffffd1 ffffffd2 ffffffd3 ffffffd4 ffffffd5 ffffffd6
  //   ffffffd7 ffffffd8 ffffffd9 ffffffda ffffffdb ffffffdc ffffffdd ffffffde ffffffdf ffffffe0 ffffffe1
  //   ffffffe2 ffffffe3 ffffffe4 ffffffe5 ffffffe6 ffffffe7 ffffffe8 ffffffe9 ffffffea ffffffeb ffffffec
  //   ffffffed ffffffee ffffffef fffffff0 fffffff1 fffffff2 fffffff3 fffffff4 fffffff5 fffffff6 fffffff7
  //   fffffff8 fffffff9 fffffffa fffffffb fffffffc fffffffd fffffffe ffffffff 0 1 2 3 4 5 6 7 8 9 a b c d
  //   e f 10 11 12 13 14 15 16 17 18 19 1a 1b 1c 1d 1e 1f 20 21 22 23 24 25 26 27 28 29 2a 2b 2c 2d 2e 2f
  //   30 31 32 33 34 35 36 37 38 39 3a 3b 3c 3d 3e 3f 40 41 42 43 44 45 46 47 48 49 4a 4b 4c 4d 4e 4f 50
  //   51 52 53 54 55 56 57 58 59 5a 5b 5c 5d 5e 5f 60 61 62 63 64 65 66 67 68 69 6a 6b 6c 6d 6e 6f 70 71
  //   72 73 74 75 76 77 78 79 7a 7b 7c 7d 7e 7f ffffff80 ffffff81 ffffff82 ffffff83 ffffff84 ffffff85
  //   ffffff86 ffffff87 ffffff88 ffffff89 ffffff8a ffffff8b ffffff8c ffffff8d ffffff8e ffffff8f ffffff90
  //   ffffff91 ffffff92 ffffff93 ffffff94 ffffff95 ffffff96 ffffff97 ffffff98 ffffff99 ffffff9a ffffff9b
  //   ffffff9c ffffff9d ffffff9e ffffff9f ffffffa0 ffffffa1 ffffffa2 ffffffa3 ffffffa4 ffffffa5 ffffffa6
  //   ffffffa7 ffffffa8 ffffffa9 ffffffaa ffffffab ffffffac ffffffad ffffffae ffffffaf ffffffb0 ffffffb1
  //   ffffffb2 ffffffb3 ffffffb4 ffffffb5 ffffffb6 ffffffb7 ffffffb8 ffffffb9 ffffffba ffffffbb ffffffbc
  //   ffffffbd ffffffbe ffffffbf ffffffc0 ffffffc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
  //   输出引脚区
endmodule

module BusModel (
  input  [31:0] WriteAddr,
  input  [31:0] WriteData,
  input  R,
  input  W,
  input  [31:0] IORead,
  input  [31:0] MemRead,
  output [31:0] ReadData,
  output out_8,
  output IOEn,
  output [11:0] IOAddr12,
  output [31:0] IOWriteData,
  output [31:0] MemAddr,
  output MemR,
  output MemW,
  output [31:0] MemWriteData
);

  wire and_2_out, and_3_out, and_4_out, and_5_out, comparator_1_eq, is_MemAddr, or_1_out, or_2_out;

  // Probe on WriteAddr
  assign MemW = is_MemAddr ? W : 1'bz;  // Controlled_Buffer controlled_buffer_1
  Comparator #(.width(20), .mode("unsigned")) comparator_1 (
    .a(WriteAddr[31:12]), .b({20{1'b1}}), .eq(comparator_1_eq));  // open: gt, lt
  assign MemR = is_MemAddr ? R : 1'bz;  // Controlled_Buffer controlled_buffer_2
  // Probe on comparator_1_eq
  not not_1 (is_MemAddr, comparator_1_eq);
  or or_1 (or_1_out, R, W);
  and and_1 (IOEn, comparator_1_eq, or_2_out);
  or or_2 (or_2_out, R, W);
  and and_2 (and_2_out, is_MemAddr, or_1_out);
  // Probe on WriteAddr
  assign MemAddr = and_2_out ? WriteAddr : 32'bz;  // Controlled_Buffer controlled_buffer_3
  // Probe on MemAddr
  and and_3 (and_3_out, is_MemAddr, W);
  assign MemWriteData = and_3_out ? WriteData : 32'bz;  // Controlled_Buffer controlled_buffer_4
  and and_4 (and_4_out, R, IOEn);
  assign ReadData = and_4_out ? IORead : 32'bz;  // Controlled_Buffer controlled_buffer_5
  assign ReadData = and_5_out ? MemRead : 32'bz;  // Controlled_Buffer controlled_buffer_6
  and and_5 (and_5_out, R, is_MemAddr);
  // Probe on ReadData

  assign IOAddr12 = WriteAddr[11:0];
  assign IOWriteData = WriteData;

  // Other names for the same wires on the sheet: IORW = out_8; RW = out_8
endmodule

module LEDDriver (
  input  in_1,
  input  IOEn,
  input  [31:0] IOWriteData,
  input  [11:0] IOAddr12,
  output [23:0] LED0
);

  wire and_1_out, comparator_1_eq;
  wire [31:0] multiplexer_1_out;

  Comparator #(.width(12), .mode("unsigned")) comparator_1 (
    .a(12'h60), .b(IOAddr12), .eq(comparator_1_eq));  // open: gt, lt
  // Probe on IOEn
  // Probe on and_1_out
  and and_1 (and_1_out, comparator_1_eq, IOEn);
  Multiplexer #(.select(1), .width(32), .disabled("Z"), .enable("false")) multiplexer_1 (
    .in1(IOWriteData), .out(multiplexer_1_out), .sel(and_1_out));  // open: in0
  // Probe on multiplexer_1_out[23:0]
  Register #(.width(24), .trigger("rising"), .Select("low")) register_1 (
    .D(multiplexer_1_out[23:0]), .en(and_1_out), .Q(LED0), .clk(in_1));  // open: clr

  // Other names for the same wires on the sheet: clk = in_1

  // Notes on the sheet:
  //   输入管脚
  //   输出管脚
endmodule

module SwitchDriver (
  input  in_1,
  input  [23:0] SW0,
  input  IOEn,
  input  [11:0] IOAddr12,
  output [31:0] IOReadData
);

  wire and_1_out, comparator_1_eq;
  wire [31:0] multiplexer_1_out;

  Comparator #(.width(12), .mode("unsigned")) comparator_1 (
    .a(12'h70), .b(IOAddr12), .eq(comparator_1_eq));  // open: gt, lt
  and and_1 (and_1_out, comparator_1_eq, IOEn);
  Multiplexer #(.select(1), .width(32), .disabled("Z"), .enable("false")) multiplexer_1 (
    .in1({{8{1'b0}}, SW0}), .out(multiplexer_1_out), .sel(and_1_out));  // open: in0
  assign IOReadData = and_1_out ? multiplexer_1_out : 32'bz;  // Controlled_Buffer controlled_buffer_1

  // Other names for the same wires on the sheet: clk = in_1

  // Notes on the sheet:
  //   输入管脚
  //   输出管脚
endmodule

module DigitDriver (
  input  in_1,
  input  IOEn,
  input  [31:0] IOWriteData,
  input  [11:0] IOAddr12,
  output [3:0] D0,
  output [3:0] D4,
  output [3:0] D1,
  output [3:0] D5,
  output [3:0] D2,
  output [3:0] D6,
  output [3:0] D3,
  output [3:0] D7
);

  wire and_1_out, comparator_1_eq;
  wire [31:0] multiplexer_1_out;

  Comparator #(.width(12), .mode("unsigned")) comparator_1 (
    .a({12{1'b0}}), .b(IOAddr12), .eq(comparator_1_eq));  // open: gt, lt
  // Probe on IOEn
  // Probe on and_1_out
  and and_1 (and_1_out, comparator_1_eq, IOEn);
  // Probe on IOWriteData
  Multiplexer #(.select(1), .width(32), .disabled("Z"), .enable("false")) multiplexer_1 (
    .in1(IOWriteData), .out(multiplexer_1_out), .sel(and_1_out));  // open: in0
  // Probe on multiplexer_1_out[3:0]
  // Probe on D0
  Register #(.width(4), .trigger("rising"), .Select("low")) register_1 (
    .D(multiplexer_1_out[3:0]), .en(and_1_out), .Q(D0), .clk(in_1));  // open: clr
  Register #(.width(4), .trigger("rising"), .Select("low")) register_2 (
    .D(multiplexer_1_out[7:4]), .en(and_1_out), .Q(D1), .clk(in_1));  // open: clr
  Register #(.width(4), .trigger("rising"), .Select("low")) register_3 (
    .D(multiplexer_1_out[11:8]), .en(and_1_out), .Q(D2), .clk(in_1));  // open: clr
  Register #(.width(4), .trigger("rising"), .Select("low")) register_4 (
    .D(multiplexer_1_out[15:12]), .en(and_1_out), .Q(D3), .clk(in_1));  // open: clr
  Register #(.width(4), .trigger("rising"), .Select("low")) register_5 (
    .D(multiplexer_1_out[19:16]), .en(and_1_out), .Q(D4), .clk(in_1));  // open: clr
  Register #(.width(4), .trigger("rising"), .Select("low")) register_6 (
    .D(multiplexer_1_out[23:20]), .en(and_1_out), .Q(D5), .clk(in_1));  // open: clr
  Register #(.width(4), .trigger("rising"), .Select("low")) register_7 (
    .D(multiplexer_1_out[27:24]), .en(and_1_out), .Q(D6), .clk(in_1));  // open: clr
  Register #(.width(4), .trigger("rising"), .Select("low")) register_8 (
    .D(multiplexer_1_out[31:28]), .en(and_1_out), .Q(D7), .clk(in_1));  // open: clr

  // Other names for the same wires on the sheet: clk = in_1

  // Notes on the sheet:
  //   输入管脚
  //   输出管脚
endmodule
